# Fritzing sketch Sunrise-Simulation-Alarm (saved by Fritzing 0.9.4)
breadboards: 2

parts:
  Part1 = Arduino Nano (Rev3.0)
  Part2 = Real Time Clock Module - DS1307 RTC Breakout Board
  U1 = LCD-16X2 [package=lcd-16x2_noholes]
  LCM1602_IIC2 = LCM1602 IIC [part_number="LCM1602 IIC" chip_label="LCM1602 IIC" package="DIP (Dual Inline) [THT]"]
  S1 = SWITCH-MOMENTARY-2 [package=tactile-pth-12mm]
  S2 = SWITCH-MOMENTARY-2 [package=tactile-pth-12mm]
  S3 = SWITCH-MOMENTARY-2 [package=tactile-pth-12mm]
  S4 = SWITCH-MOMENTARY-2 [package=tactile-pth-12mm]
  Part3 = ws2812b [package="smd 2812b"]
  R1 = Resistor [tolerance=±5% resistance=330 package=THT]
  BAT1 = LIPO-2000mAh [package=lipo-2000]
  M1 = TP4056 Module [part_number=HW-107]
  Reg1 = DC-DC CONVERTER [part_number=80633 package=dc-dc_converter]

nets:
  GND: Part1.GND, Part2.GND, LCM1602_IIC2.GND, S1.1, S2.1, S3.1, S4.1, Part3.VSS, Reg1.OUT-
  N1: Part1.D7, R1.Pin_0
  N2: Part1.D8, S1.2
  N3: Part1.D9, S4.2
  N4: Part1.D10, S3.2
  N5: Part1.D11/MOSI, S2.2
  N6: Part1.VIN, Reg1.OUT+
  5V: Part1.5V, Part2.5V, LCM1602_IIC2.VCC, Part3.VDD
  N7: Part1.A5, Part2.SDA, LCM1602_IIC2.SDA
  N8: Part1.A4, Part2.SCL, LCM1602_IIC2.SCL
  VSS: U1.VSS, LCM1602_IIC2.VSS
  VDD: U1.VDD, LCM1602_IIC2.VDD
  N9: U1.VO, LCM1602_IIC2.V0
  N10: U1.RS, LCM1602_IIC2.RS
  N11: U1.R_W, LCM1602_IIC2.RW
  N12: U1.E, LCM1602_IIC2.E
  N13: U1.DB0, LCM1602_IIC2.D0
  N14: U1.DB1, LCM1602_IIC2.D1
  N15: U1.DB2, LCM1602_IIC2.D2
  N16: U1.DB3, LCM1602_IIC2.D3
  N17: U1.DB4, LCM1602_IIC2.D4
  N18: U1.DB5, LCM1602_IIC2.D5
  N19: U1.DB6, LCM1602_IIC2.D6
  N20: U1.DB7, LCM1602_IIC2.D7
  N21: U1.A, LCM1602_IIC2.A
  N22: U1.K, LCM1602_IIC2.K
  N23: LCM1602_IIC2.LED_A, LCM1602_IIC2.LED_B
  N24: Part3.DIN, R1.Pin_1
  N25: BAT1.+, M1.BAT+
  N26: BAT1.-, M1.BAT-
  N27: M1.OUT-#1, Reg1.IN-
  N28: M1.OUT-#4, Reg1.IN+

custom parts:
  LCM1602 IIC: I2C-Module to use a 1602 or 2004 LCD on with the wire.h libory Serial LCD Modul
  TP4056 Module: TP4056 Lithium Battery Charge Management Module Links: TP4056 website
  DC-DC CONVERTER: WYHP 5A constant current/voltage manufactured by Shenzhen Weiyapuhua Technology Co., Ltd
